# Fritzing sketch PiezoRGBledUno5V (saved by Fritzing 0.9.2b)
breadboards: 1

parts:
  Piezo_element = Piezo Speaker
  part = Resistor [tolerance=±5% resistance=1M package=THT]
  RGB_led = RGB LED - (4 legs) [package="5 mm [THT]"]
  part_2 = Resistor [tolerance=±5% resistance=330 package=THT]
  part_3 = Resistor [tolerance=±5% resistance=330 package=THT]
  part_4 = Resistor [tolerance=±5% resistance=330 package=THT]
  5V_power1 = Power plug
  Part1 = Arduino Uno (Rev3) - ICSP

nets:
  GND: Piezo_element.pin1, part.Pin_0, 5V_power1.GND, Part1.GND
  N1: Piezo_element.pin2, part.Pin_1, Part1.A0
  N2: RGB_led.red_cathode, part_4.Pin_0
  VCC: RGB_led.common_anode, 5V_power1.VCC, Part1.5V
  N3: RGB_led.green_cathode, part_3.Pin_0
  N4: RGB_led.blue_cathode, part_2.Pin_0
  N5: part_2.Pin_1, Part1.D3_PWM
  N6: part_3.Pin_1, Part1.D5_PWM
  N7: part_4.Pin_1, Part1.D6_PWM
